// Logisim project 4-bit Mini ALU.circ as structural Verilog: 1 circuit, main circuit main
module main (
  input  C,
  input  Bin,
  input  [3:0] A_3_0,
  input  [3:0] B_3_0,
  input  in_5,
  input  S2,
  input  S1,
  input  S0,
  input  in_9,
  output C_OUT,
  output out_11,
  output out_12
);

  wire and_1_out, and_2_out, and_3_out, and_4_out, and_5_out, and_6_out, and_7_out, and_8_out, and_9_out,
       and_10_out, and_11_out, and_12_out, and_13_out, and_14_out, and_15_out, and_16_out, and_17_out,
       and_18_out, and_19_out, and_20_out, and_21_out, and_22_out, and_23_out, and_24_out, and_25_out,
       and_26_out, and_27_out, and_29_out, not_1_out, not_2_out, not_3_out, not_4_out, or_1_out, or_2_out,
       or_3_out, or_5_out, or_6_out, or_7_out, or_8_out, or_9_out, or_10_out, or_14_out, xor_1_out,
       xor_2_out, xor_3_out, xor_4_out, xor_9_out, xor_12_out, xor_14_out, xor_15_out, xor_19_out,
       xor_20_out, xor_21_out, xor_22_out;
  wire [0:0] and_30_out;
  wire [3:0] and_28_out, multiplexer_1_out, multiplexer_2_out, not_5_out, or_12_out, subtractor_1_out,
       xor_6_out, xor_10_out, xor_11_out, xor_25_out;

  not not_1 (not_1_out, A_3_0[0]);
  not not_2 (not_2_out, A_3_0[1]);
  not not_3 (not_3_out, A_3_0[2]);
  not not_4 (not_4_out, A_3_0[3]);
  xor xor_1 (xor_1_out, A_3_0[0], B_3_0[0]);
  xor xor_2 (xor_2_out, A_3_0[1], B_3_0[1]);
  and and_1 (and_1_out, not_2_out, B_3_0[1]);
  and and_2 (and_2_out, not_2_out, or_1_out);
  and and_3 (and_3_out, B_3_0[1], or_1_out);
  xor xor_3 (xor_3_out, A_3_0[2], B_3_0[2]);
  and and_4 (and_4_out, not_3_out, B_3_0[2]);
  and and_5 (and_5_out, not_3_out, or_2_out);
  and and_6 (and_6_out, B_3_0[2], or_2_out);
  xor xor_4 (xor_4_out, A_3_0[3], B_3_0[3]);
  and and_7 (and_7_out, not_4_out, B_3_0[3]);
  and and_8 (and_8_out, not_4_out, or_3_out);
  and and_9 (and_9_out, B_3_0[3], or_3_out);
  and and_10 (and_10_out, not_1_out, B_3_0[0]);
  and and_11 (and_11_out, not_1_out, Bin);
  and and_12 (and_12_out, B_3_0[0], Bin);
  xor xor_5 (xor_6_out[3], xor_4_out, or_3_out);
  xor xor_6 (xor_6_out[0], xor_1_out, Bin);
  or or_1 (or_1_out, and_10_out, and_11_out, and_12_out);
  xor xor_7 (xor_6_out[1], xor_2_out, or_1_out);
  or or_2 (or_2_out, and_1_out, and_2_out, and_3_out);
  xor xor_8 (xor_6_out[2], xor_3_out, or_2_out);
  or or_3 (or_3_out, and_4_out, and_5_out, and_6_out);
  or or_4 (out_12, and_7_out, and_8_out, and_9_out);
  and and_13 (and_13_out, C, xor_9_out);
  xor xor_9 (xor_9_out, B_3_0[0], A_3_0[0]);
  xor xor_10 (xor_10_out[0], C, xor_9_out);
  or or_5 (or_5_out, and_13_out, and_14_out);
  xor xor_11 (xor_11_out[0], xor_12_out, in_9);
  xor xor_12 (xor_12_out, A_3_0[0], 1'b1);
  and and_14 (and_14_out, B_3_0[0], A_3_0[0]);
  or or_6 (or_6_out, and_15_out, and_16_out);
  and and_15 (and_15_out, 1'b1, A_3_0[0]);
  and and_16 (and_16_out, xor_12_out, in_9);
  and and_17 (and_17_out, or_5_out, xor_15_out);
  xor xor_13 (xor_11_out[1], xor_14_out, or_6_out);
  xor xor_14 (xor_14_out, A_3_0[1], 1'b0);
  xor xor_15 (xor_15_out, B_3_0[1], A_3_0[1]);
  xor xor_16 (xor_10_out[1], or_5_out, xor_15_out);
  or or_7 (or_7_out, and_17_out, and_19_out);
  or or_8 (or_8_out, and_18_out, and_20_out);
  and and_18 (and_18_out, 1'b0, A_3_0[1]);
  and and_19 (and_19_out, B_3_0[1], A_3_0[1]);
  and and_20 (and_20_out, xor_14_out, or_6_out);
  xor xor_17 (xor_10_out[2], or_7_out, xor_20_out);
  and and_21 (and_21_out, or_7_out, xor_20_out);
  xor xor_18 (xor_11_out[2], xor_19_out, or_8_out);
  xor xor_19 (xor_19_out, A_3_0[2], 1'b0);
  xor xor_20 (xor_20_out, B_3_0[2], A_3_0[2]);
  and and_22 (and_22_out, B_3_0[2], A_3_0[2]);
  or or_9 (or_9_out, and_21_out, and_22_out);
  or or_10 (or_10_out, and_23_out, and_24_out);
  and and_23 (and_23_out, 1'b0, A_3_0[2]);
  and and_24 (and_24_out, xor_19_out, or_8_out);
  and and_25 (and_25_out, or_9_out, xor_22_out);
  xor xor_21 (xor_21_out, A_3_0[3], 1'b0);
  xor xor_22 (xor_22_out, B_3_0[3], A_3_0[3]);
  xor xor_23 (xor_10_out[3], or_9_out, xor_22_out);
  or or_11 (C_OUT, and_25_out, and_27_out);
  xor xor_24 (xor_11_out[3], xor_21_out, or_10_out);
  and and_26 (and_26_out, 1'b0, A_3_0[3]);
  and and_27 (and_27_out, B_3_0[3], A_3_0[3]);
  assign and_28_out = A_3_0 & B_3_0;  // AND_Gate and_28, 4 bits wide
  assign or_12_out = A_3_0 | B_3_0;  // OR_Gate or_12, 4 bits wide
  assign xor_25_out = A_3_0 ^ B_3_0;  // XOR_Gate xor_25, 4 bits wide
  assign not_5_out = ~A_3_0;  // NOT_Gate not_5, 4 bits wide
  or or_13 (out_11, and_26_out, and_29_out);
  and and_29 (and_29_out, xor_21_out, or_10_out);
  Multiplexer #(.select(3), .width(4)) multiplexer_1 (
    .in0(xor_10_out), .in1(xor_6_out), .in2(and_28_out), .in3(or_12_out), .in4(xor_25_out), .in5(not_5_out),
    .in6(xor_11_out), .in7(4'b0000), .out(multiplexer_1_out), .sel({S2, S1, S0}), .en(in_5));
  or or_14 (or_14_out, multiplexer_1_out[1], multiplexer_1_out[2]);
  Subtractor #(.width(4)) subtractor_1 (.a(multiplexer_1_out), .b(4'b1010), .out(subtractor_1_out));  // open: bin, bout
  and and_30 (and_30_out[0], or_14_out, multiplexer_1_out[3]);
  Multiplexer #(.width(4)) multiplexer_2 (
    .in0(multiplexer_1_out), .in1(subtractor_1_out), .out(multiplexer_2_out), .sel(and_30_out[0]));  // open: en
  Hex_Digit_Display hex_digit_display_1 (.value({3'b000, and_30_out[0]}));  // open: dp
  Hex_Digit_Display hex_digit_display_2 (.value(multiplexer_2_out));  // open: dp

  // Notes on the sheet:
  //   4-bit Ripple
  //   Carry Subtractor
  //   A0
  //   B0
  //   A1
  //   B1
  //   A2
  //   B2
  //   A3
  //   B3
  //   4-bit Mini ALU
  //   With Operations like Add , Sub
  //   AND , OR , INC , ZERO.
  //   B0
  //   C1
  //   A
  //   B
  //   A0
  //   A0
  //               S0
  //   B0
  //   C
  //   B1
  //   C2
  //   A1
  //   B1
  //   4-bit Ripple Carry Adder
  //   A
  //   A1
  //               S1
  //   4bit Inputs
  //   A & B are two operands
  //   of this ALU
  //   A
  //   C
  //   A2
  //   4-bit Ripple Carry Adder
  //   B2
  //               S2
  //   C3
  //   B
  //   B2
  //   B
  //   A2
  //   B3
  //   A3
  //   A3
  //   B3
  //               S3
  //   3bit
  //   OPCode
  //   Mux Inputs
  //   I0 , I1 , I2 ... I7
  //   OP[2:0] = S2 , S1 , S0
  //   OPCode Mappings
  //   000 -> ADD
  //   001 -> SUB
  //   010 -> AND
  //   011 -> OR
  //   100 -> XOR
  //   101 -> NOT
  //   110 -> INC
  //   111 -> ZERO
  //   Units =
  //   a = 10
  //   Tens = R3 AND (R1 OR R2)
  //   Spitter
  //   index 0 = R0
  //   index 1 = R1
  //   index 2 = R2
  //   index 3 = R3
  //   If Tens == 0 do R - 10 else R
endmodule
