// Logisim project Half_Adder.circ as structural Verilog: 1 circuit, main circuit main
module main (
  input  in_1,
  input  in_2,
  input  in_3,
  input  in_4,
  input  in_5,
  input  in_6,
  output out_7,
  output out_8,
  output out_9,
  output out_10,
  output out_11,
  output out_12
);

  wire and_2_out, and_3_out, nand_1_out, nand_2_out, nand_3_out, nand_4_out, not_1_out, not_2_out;

  not not_1 (not_1_out, in_6);
  not not_2 (not_2_out, in_5);
  xor xor_1 (out_7, in_1, in_2);
  and and_1 (out_9, in_1, in_2);
  and and_2 (and_2_out, in_5, not_1_out);
  and and_3 (and_3_out, not_2_out, in_6);
  and and_4 (out_12, in_5, in_6);
  or or_1 (out_11, and_2_out, and_3_out);
  nand nand_1 (nand_1_out, in_3, in_4);
  nand nand_2 (nand_2_out, in_3, in_4);
  nand nand_3 (nand_3_out, in_3, nand_1_out);
  nand nand_4 (nand_4_out, nand_1_out, in_4);
  nand nand_5 (out_10, nand_2_out, nand_2_out);
  nand nand_6 (out_8, nand_3_out, nand_3_out, nand_4_out);

  // Notes on the sheet:
  //                                                 1)  Half Adder using Xor & And Gate
  //                                                                      HALF-ADDER
  //   3)  Half Adder Using Basic Gates ( 3 And 2 OR Gates)                                                                     
  //   2)  Half Adder Using Universal Gates ( 6 AND Gates)                                                                           
endmodule
