// Logisim project basic_gates.circ as structural Verilog: 1 circuit, main circuit main
module main (
  input  in_1,
  input  in_2,
  input  in_3,
  input  in_4,
  input  in_5,
  input  in_6,
  input  in_7,
  input  in_8,
  input  in_9,
  input  in_10,
  input  in_11,
  input  A,
  input  A_2,
  input  B,
  input  B_2,
  input  A_3,
  input  B_3,
  output out_18,
  output out_19,
  output out_20,
  output out_21,
  output out_22,
  output out_23,
  output out_24
);

  wire and_1_out, and_2_out, and_3_out, and_4_out, and_5_out, nand_1_out, nand_2_out, nand_3_out, nand_5_out,
       nand_6_out, nand_9_out, nand_10_out, nand_11_out, nand_12_out, nand_14_out, not_1_out, not_2_out;

  nand nand_1 (nand_1_out, A_2, B);
  nand nand_2 (nand_2_out, A_3, B_3);
  nand nand_3 (nand_3_out, in_1, in_2);
  nand nand_4 (out_19, in_5, in_5);
  nand nand_5 (nand_5_out, in_6, in_6);
  nand nand_6 (nand_6_out, in_10, in_10);
  nand nand_7 (out_18, nand_3_out, nand_3_out);
  nand nand_8 (out_21, nand_5_out, nand_6_out);
  nand nand_9 (nand_9_out, A_2, nand_1_out);
  nand nand_10 (nand_10_out, nand_1_out, B);
  nand nand_11 (nand_11_out, A_3, nand_2_out);
  nand nand_12 (nand_12_out, nand_2_out, B_3);
  nand nand_13 (out_22, nand_9_out, nand_10_out);
  nand nand_14 (nand_14_out, nand_11_out, nand_12_out);
  not nand_15 (out_24, nand_14_out);  // NAND_Gate
  and and_1 (and_1_out, in_3, in_4);
  and and_2 (and_2_out, in_7, in_8);
  and and_3 (and_3_out, in_9, in_11);
  not not_1 (not_1_out, B_2);
  not not_2 (not_2_out, A);
  and and_4 (and_4_out, A, not_1_out);
  and and_5 (and_5_out, not_2_out, B_2);
  or or_1 (out_20, and_1_out, and_2_out, and_3_out);
  or or_2 (out_23, and_4_out, and_5_out);

  // Notes on the sheet:
  //   B * (A * B ) ^ T
  //   B * (A * B ) ^ T
  //   A  * (A * B) ^ T
  //   (B * ( A * B ) ^ T ) ^ T
  //   (B * ( A * B ) ^ T ) ^ T
  //   (A * ( A * B ) ^ T) ^ T
  //   (A + B ) ( A * B ) ^ T
  //   (A + B ) ( A * B ) ^ T
  //   B'
  //   A'
  //   XOR Gate Using Basic Gates
endmodule
