// Logisim project xor_gate.circ as structural Verilog: 1 circuit, main circuit main
module main (
  input  in_1,
  input  in_2,
  input  in_3,
  input  in_4,
  output out_5,
  output out_6
);

  wire and_1_out, and_2_out, nand_1_out, nand_2_out, nand_3_out, not_1_out, not_2_out;

  nand nand_1 (nand_1_out, in_3, in_4);
  nand nand_2 (nand_2_out, in_3, nand_1_out);
  nand nand_3 (nand_3_out, nand_1_out, in_4);
  nand nand_4 (out_6, nand_2_out, nand_3_out);
  not not_1 (not_1_out, in_1);
  not not_2 (not_2_out, in_2);
  and and_1 (and_1_out, in_1, not_2_out);
  and and_2 (and_2_out, not_1_out, in_2);
  or or_1 (out_5, and_1_out, and_2_out);

  // Notes on the sheet:
  //                                          Xor Using 4 Nand gates
  //                         XOR GATE
  //                               BE : AB' + A'B
  //                                                                               Xor Using Basic Gates
endmodule
