// Logisim project Full_Adder.circ as structural Verilog: 1 circuit, main circuit main
module main (
  input  A,
  input  B,
  input  C,
  input  A_2,
  input  B_2,
  input  C_2,
  output out_7,
  output out_8,
  output SUM,
  output CARRY
);

  wire and_1_out, and_2_out, and_3_out, and_4_out, and_5_out, and_6_out, and_7_out, and_8_out, not_1_out,
       not_2_out, not_3_out, not_4_out, or_2_out, xor_1_out;

  xor xor_1 (xor_1_out, A, B);
  and and_1 (and_1_out, B, A);
  xor xor_2 (out_7, xor_1_out, C);
  and and_2 (and_2_out, xor_1_out, C);
  not not_1 (not_1_out, A_2);
  not not_2 (not_2_out, B_2);
  and and_3 (and_3_out, A_2, not_2_out);
  and and_4 (and_4_out, not_1_out, B_2);
  and and_5 (and_5_out, A_2, B_2);
  or or_1 (out_8, and_2_out, and_1_out);
  or or_2 (or_2_out, and_3_out, and_4_out);
  not not_3 (not_3_out, or_2_out);
  not not_4 (not_4_out, C_2);
  and and_6 (and_6_out, or_2_out, C_2);
  and and_7 (and_7_out, or_2_out, not_4_out);
  and and_8 (and_8_out, not_3_out, C_2);
  or or_3 (CARRY, and_6_out, and_5_out);
  or or_4 (SUM, and_7_out, and_8_out);

  // Notes on the sheet:
  //   Full-Adder Using 2 XOR & 2 AND & 1 OR Gates!!                    
  //               SUM
  //                       Sum = A (+) B (+) C
  //                                 Carry = A*B + C * ( A (+) B )
  //   Full-Adder                                            
  //   CARRY
  //   Full-Adder Using 6 AND & 3 OR & 4 OR Gates!!
endmodule
