// Logisim project Full_Subtractor.circ as structural Verilog: 1 circuit, main circuit main
module main (
  input  A,
  input  A_2,
  input  B,
  input  C,
  input  B_2,
  input  in_6,
  input  in_7,
  input  B_3,
  input  C_2,
  output Diff,
  output out_11,
  output out_12,
  output Borrow,
  output out_14,
  output Borrow_2
);

  wire and_1_out, and_2_out, and_3_out, and_4_out, and_5_out, and_6_out, and_7_out, and_8_out, nand_1_out,
       nand_2_out, nand_3_out, nand_4_out, nand_5_out, nand_6_out, nand_7_out, nand_8_out, nand_9_out,
       nand_10_out, nand_11_out, nand_12_out, nand_14_out, nand_15_out, nand_16_out, not_1_out, not_2_out,
       not_3_out, not_4_out, not_5_out, not_6_out, not_7_out, not_8_out, or_2_out, xor_1_out;

  xor xor_1 (xor_1_out, A_2, B_2);
  not not_1 (not_1_out, A_2);
  not not_2 (not_2_out, xor_1_out);
  nand nand_1 (nand_1_out, in_7, B_3);
  xor xor_2 (out_11, xor_1_out, in_6);
  and and_1 (and_1_out, not_2_out, in_6);
  and and_2 (and_2_out, not_1_out, B_2);
  nand nand_2 (nand_2_out, in_7, nand_1_out);
  nand nand_3 (nand_3_out, nand_1_out, B_3);
  or or_1 (Borrow, and_1_out, and_2_out);
  nand nand_4 (nand_4_out, nand_2_out, nand_3_out);
  nand nand_5 (nand_5_out, in_7, in_7);
  nand nand_6 (nand_6_out, nand_5_out, B_3);
  not not_3 (not_3_out, B);
  not not_4 (not_4_out, A);
  and and_3 (and_3_out, A, not_3_out);
  and and_4 (and_4_out, not_4_out, B);
  nand nand_7 (nand_7_out, nand_6_out, nand_6_out);
  not not_5 (not_5_out, A);
  nand nand_8 (nand_8_out, nand_4_out, C_2);
  or or_2 (or_2_out, and_3_out, and_4_out);
  nand nand_9 (nand_9_out, nand_4_out, nand_8_out);
  nand nand_10 (nand_10_out, nand_8_out, C_2);
  nand nand_11 (nand_11_out, nand_4_out, nand_4_out);
  and and_5 (and_5_out, not_5_out, B);
  nand nand_12 (nand_12_out, nand_11_out, C_2);
  not not_6 (not_6_out, C);
  not not_7 (not_7_out, or_2_out);
  not not_8 (not_8_out, or_2_out);
  nand nand_13 (out_14, nand_9_out, nand_10_out);
  and and_6 (and_6_out, or_2_out, not_6_out);
  and and_7 (and_7_out, not_7_out, C);
  nand nand_14 (nand_14_out, nand_12_out, nand_12_out);
  nand nand_15 (nand_15_out, nand_14_out, nand_14_out);
  nand nand_16 (nand_16_out, nand_7_out, nand_7_out);
  or or_3 (Diff, and_6_out, and_7_out);
  and and_8 (and_8_out, not_8_out, C);
  nand nand_17 (Borrow_2, nand_15_out, nand_16_out);
  or or_4 (out_12, and_8_out, and_5_out);

  // Notes on the sheet:
  //   C
  //           B. = Bin ( A (+) B )' + A' . B
  //   A
  //   Full-Subtractor                      
  //   Sample Eq's
  //   Diff = A (+) B (+) Bin
  //   Diff
  //   Using Only Universal NAND Gate ( 17 NAND Gates )
  //   Using Only Basic Gates ( 6 AND Gates & 3 OR Gates & 6 NOT Gates)
  //   Diff
  //   Borrow
endmodule
