// Logisim project Half_Adder.circ as structural Verilog: 1 circuit, main circuit main
module main (
  input  in_1,
  input  in_2,
  input  in_3,
  input  in_4,
  output out_5,
  output out_6,
  output out_7,
  output out_8
);

  wire nand_1_out, nand_2_out, nand_3_out, nand_4_out;

  xor xor_1 (out_5, in_1, in_2);
  and and_1 (out_7, in_1, in_2);
  nand nand_1 (nand_1_out, in_3, in_4);
  nand nand_2 (nand_2_out, in_3, in_4);
  nand nand_3 (nand_3_out, in_3, nand_1_out);
  nand nand_4 (nand_4_out, nand_1_out, in_4);
  nand nand_5 (out_8, nand_2_out, nand_2_out);
  nand nand_6 (out_6, nand_3_out, nand_3_out, nand_4_out);

  // Notes on the sheet:
  //                                                   Half Adder using Xor & And Gate
  //                                                                      HALF-ADDER
  //   Half Adder Using Universal Gates ( 6 AND Gates)                                                                           
endmodule
