// Logisim project half_subtractor.circ as structural Verilog: 1 circuit, main circuit main
module main (
  input  in_1,
  input  B,
  input  A,
  input  B_2,
  input  A_2,
  input  B_3,
  output Diff,
  output Diff_2,
  output Borrow,
  output Borrow_2,
  output Diff_3,
  output Borrow_3
);

  wire and_2_out, and_3_out, nand_1_out, nand_2_out, nand_3_out, nand_4_out, nand_5_out, not_1_out,
       not_2_out, not_3_out, not_4_out;

  not not_1 (not_1_out, in_1);
  xor xor_1 (Diff, in_1, B);
  and and_1 (Borrow, not_1_out, B);
  not not_2 (not_2_out, B_3);
  not not_3 (not_3_out, A_2);
  not not_4 (not_4_out, A_2);
  and and_2 (and_2_out, A_2, not_2_out);
  and and_3 (and_3_out, not_3_out, B_3);
  and and_4 (Borrow_3, not_4_out, B_3);
  or or_1 (Diff_3, and_2_out, and_3_out);
  nand nand_1 (nand_1_out, A, B_2);
  nand nand_2 (nand_2_out, A, nand_1_out);
  nand nand_3 (nand_3_out, nand_1_out, B_2);
  nand nand_4 (nand_4_out, A, A);
  nand nand_5 (nand_5_out, nand_4_out, B_2);
  nand nand_6 (Diff_2, nand_2_out, nand_3_out);
  nand nand_7 (Borrow_2, nand_5_out, nand_5_out);

  // Notes on the sheet:
  //   A
  //                  B = A' * B
  //            Sample Eq:
  //   D = A (+) B
  //   A (+) B
  //   A'
  //   B
  //                                                3 AND gates , 3 NOT gates , 1 OR gates.
  //   Implementation of half-subtractor using only basic gates.
  //   A'*B
  //   Half-Subtractor
  //                                                              7 nand gates
  //   B
  //   A
  //   (A . B)'
  //   (A . B)'
  //   B
  //   A'
  //   Implementation of half-subtractor using only universal gates
  //   (A . ( A . B )')'
  //   (B . ( A . B )')'
  //   A'*B
  //   A (+) B
endmodule
